# Fritzing sketch leo2mdx (saved by Fritzing 0.9.3b)
breadboards: 1

parts:
  IC1 = IC, DIP package, 20 pins [chip_label=MAX233]
  C1 = Electrolytic Capacitor [capacitance=0.1mF package="100 mil [THT, electrolytic]"]
  Part4 = DB25M
  Part5 = Arduino Leonardo (Rev3b)

nets:
  N1: IC1.pin1, Part5.D3_PWM/SCL
  N2: IC1.pin2, Part5.D1/TX
  N3: IC1.pin3, Part5.D0/RX
  N4: IC1.pin4, Part4.pin2
  N5: IC1.pin5, Part4.pin3
  N6: IC1.pin6, C1.+, Part5.GND
  N7: IC1.pin7, C1.-, Part5.5V
  N8: IC1.pin9, Part4.pin7
  N9: IC1.pin10, IC1.pin16
  N10: IC1.pin11, IC1.pin15
  N11: IC1.pin18, Part4.pin6
  N12: IC1.pin19, Part4.pin20
  N13: IC1.pin20, Part5.D2/SDA

// code stored in the sketch: leo2mdx.ino
/* 
now using DTR flow control
*/

boolean local_echo = false;
boolean wait_echo = false;

int DSR_pin = 3;
int DTR_pin = 2; 
int led_pin = 13;

boolean waiting = false;

void setup() {
  // initialize both serial ports:
  Serial.begin(9600);
  Serial1.begin(9600);

  // RTS
  pinMode(DSR_pin, OUTPUT);
  
  // CTS 
  pinMode(DTR_pin, INPUT);

  pinMode(led_pin, OUTPUT);

  // set RTS
  digitalWrite(DSR_pin, HIGH);
}

void loop() {
  // read from port 1, send to port 0:
  if (Serial1.available()) {
    int inByte = Serial1.read();
    Serial.write(inByte); 
  }
  
  // read from port 0, send to port 1:
  if (Serial.available()) {
    //flushing here might send a char after DTR change
    //but we checked DTR at the last read so it should be ok
    //Serial1.flush();
    if (digitalRead(DTR_pin)==LOW) {
      digitalWrite(led_pin,LOW);
      int inByte = Serial.read();
      Serial1.write(inByte);
      if (local_echo && Serial) Serial.write(inByte);
      Serial1.flush();
      waiting = false;
    } else {
      // DTR high
      digitalWrite(led_pin,HIGH);
      if (wait_echo && !waiting && Serial) Serial.write("<---WAIT--->");
      waiting = true;
    }
  } 
}
